# Fritzing sketch arduino-LED-display-2x7segments (saved by Fritzing 0.9.1b)
breadboards: 1

parts:
  Součástka1 = Arduino Leonardo (Rev3b)
  DA56-11GWA = 2 Digit 7 Segment LED CC Display RED
  R1 = Resistor [tolerance=±5% resistance=150 package=THT]
  74HC164 = SN74LS32N [package="DIP14 [THT]"]
  74HC164_2 = SN74LS32N [package="DIP14 [THT]"]

nets:
  VCC: Součástka1.5V, 74HC164.Vcc, 74HC164_2.Vcc
  GND: Součástka1.GND, 74HC164.GND, 74HC164_2.GND
  N1: Součástka1.D9_PWM/A9, R1.Pin_1
  N2: Součástka1.D10_PWM/A10, 74HC164.3Y, 74HC164_2.3Y
  N3: Součástka1.D11_PWM, 74HC164.3A, 74HC164_2.3A
  N4: Součástka1.D12/A11, 74HC164.1A, 74HC164.1B
  N5: DA56-11GWA.pin1, 74HC164_2.1Y
  N6: DA56-11GWA.pin2, 74HC164_2.2A
  N7: DA56-11GWA.pin3, 74HC164_2.2Y
  N8: DA56-11GWA.pin4, 74HC164_2.3B
  N9: DA56-11GWA.pin5, 74HC164.1Y
  N10: DA56-11GWA.pin6, 74HC164.2A
  N11: DA56-11GWA.pin7, 74HC164.2B
  N12: DA56-11GWA.pin8, 74HC164.2Y
  N13: DA56-11GWA.pin9, 74HC164.3B
  N14: DA56-11GWA.pin10, 74HC164.4A
  N15: DA56-11GWA.pin11, 74HC164.4Y
  N16: DA56-11GWA.pin12, 74HC164.4B, 74HC164_2.1A, 74HC164_2.1B
  N17: DA56-11GWA.pin13, DA56-11GWA.pin14, R1.Pin_0
  N18: DA56-11GWA.pin15, 74HC164_2.4A
  N19: DA56-11GWA.pin16, 74HC164_2.4Y
  N20: DA56-11GWA.pin17, 74HC164_2.2B
  N21: DA56-11GWA.pin18, 74HC164_2.4B

custom parts:
  2 Digit 7 Segment LED CC Display RED: 2 digit 7 segment LED display RED
